// Logisim project new_arc.circ as structural Verilog: 4 circuits, main circuit main
module main (
);

  _8bit_reg u_8bit_reg_1 ();  // open: in_1, in_2, in_3, out_5, in_4
  _8bit_reg u_8bit_reg_2 ();  // open: in_1, in_2, in_3, out_5, in_4
  ALU alu_1 ();  // open: in_1, INV_X, in_3, INV_Y, in_5, INV_out, in_7, out_8
endmodule

module _8bit_reg (
  input  [7:0] in_1,
  input  in_2,
  input  in_3,
  input  in_4,
  output [7:0] out_5
);

  wire and_1_out;
  wire [7:0] d_ff_1_q;

  and and_1 (and_1_out, in_2, in_3);
  D_Flip_Flop #(.trigger("falling")) d_ff_1 (
    .clk(and_1_out), .D(in_1[0]), .Q(d_ff_1_q[0]));  // open: Qn, preset, en, reset
  D_Flip_Flop #(.trigger("falling")) d_ff_2 (
    .clk(and_1_out), .D(in_1[1]), .Q(d_ff_1_q[1]));  // open: Qn, preset, en, reset
  D_Flip_Flop #(.trigger("falling")) d_ff_3 (
    .clk(and_1_out), .D(in_1[2]), .Q(d_ff_1_q[2]));  // open: Qn, preset, en, reset
  D_Flip_Flop #(.trigger("falling")) d_ff_4 (
    .clk(and_1_out), .D(in_1[3]), .Q(d_ff_1_q[3]));  // open: Qn, preset, en, reset
  D_Flip_Flop #(.trigger("falling")) d_ff_5 (
    .clk(and_1_out), .D(in_1[4]), .Q(d_ff_1_q[4]));  // open: Qn, preset, en, reset
  D_Flip_Flop #(.trigger("falling")) d_ff_6 (
    .clk(and_1_out), .D(in_1[5]), .Q(d_ff_1_q[5]));  // open: Qn, preset, en, reset
  D_Flip_Flop #(.trigger("falling")) d_ff_7 (
    .clk(and_1_out), .D(in_1[6]), .Q(d_ff_1_q[6]));  // open: Qn, preset, en, reset
  D_Flip_Flop #(.trigger("falling")) d_ff_8 (
    .clk(and_1_out), .D(in_1[7]), .Q(d_ff_1_q[7]));  // open: Qn, preset, en, reset
  assign out_5 = in_4 ? d_ff_1_q : 8'bz;  // Controlled_Buffer controlled_buffer_1
endmodule

module ALU (
  input  [7:0] in_1,
  input  INV_X,
  input  [7:0] in_3,
  input  INV_Y,
  input  [1:0] in_5,
  input  INV_out,
  input  in_7,
  output [7:0] out_8
);

  wire [7:0] adder_1_out, controled_inv_1_out_3, controled_inv_2_out_3, controled_inv_3_out_3,
       multiplexer_1_out;

  controled_inv controled_inv_1 (.in_1(in_1), .in_2(INV_X), .out_3(controled_inv_1_out_3));
  controled_inv controled_inv_2 (.in_1(in_3), .in_2(INV_Y), .out_3(controled_inv_2_out_3));
  Adder adder_1 (.a(controled_inv_1_out_3), .b(controled_inv_2_out_3), .out(adder_1_out));  // open: cin, cout
  Multiplexer #(.select(2), .width(8)) multiplexer_1 (
    .in0(adder_1_out), .out(multiplexer_1_out), .sel(in_5), .en(in_7));  // open: in1, in2, in3
  controled_inv controled_inv_3 (.in_1(multiplexer_1_out), .in_2(INV_out), .out_3(controled_inv_3_out_3));
  assign out_8 = in_7 ? controled_inv_3_out_3 : 8'bz;  // Controlled_Buffer controlled_buffer_1

  // Notes on the sheet:
  //   X
  //   Y
endmodule

module controled_inv (
  input  [7:0] in_1,
  input  in_2,
  output [7:0] out_3
);

  xor xor_1 (out_3[0], in_1[0], in_2);
  xor xor_2 (out_3[1], in_1[1], in_2);
  xor xor_3 (out_3[2], in_1[2], in_2);
  xor xor_4 (out_3[3], in_1[3], in_2);
  xor xor_5 (out_3[4], in_1[4], in_2);
  xor xor_6 (out_3[5], in_1[5], in_2);
  xor xor_7 (out_3[6], in_1[6], in_2);
  xor xor_8 (out_3[7], in_1[7], in_2);
endmodule
